# Fritzing sketch ch15_2wheel_robot_circuit (saved by Fritzing 1.0.8)
breadboards: 1

parts:
  VCC1 = Battery
  Part1 = Arduino Uno (Rev3) - ICSP
  PWMA = Motor Driver 1A Dual TB6612FNG
  M1 = gear-motor
  M2 = gear-motor

nets:
  GND: VCC1.-, Part1.GND, PWMA.GND
  N1: VCC1.+, Part1.VIN, PWMA.VM
  N2: Part1.D8, PWMA.BIN2
  N3: Part1.D9_PWM, PWMA.PWMB
  N4: Part1.D11_PWM/MOSI, PWMA.PWMA
  N5: Part1.D4, PWMA.AIN2
  N6: Part1.D5_PWM, PWMA.AIN1
  N7: Part1.D6_PWM, PWMA.STBY
  N8: Part1.D7, PWMA.BIN1
  5V: Part1.5V, PWMA.VCC
  N9: PWMA.B02, M1.pin_2
  N10: PWMA.A02, M2.pin_1
  N11: PWMA.A01, M2.pin_2

custom parts:
  Battery: Your standard 2x 18650 battery pack (7.4 Volts)
