# Fritzing sketch ch15_2wheel_robot_circuit_l298p (saved by Fritzing 1.0.8)

parts:
  VCC1 = Battery  # not connected
  M1 = gear-motor
  M2 = gear-motor
  MOTOR_SHIELD1 = FunduMoto Keyes L298P Motor Shield [package="Arduino shield"]

nets:
  N1: M1.pin_1, MOTOR_SHIELD1.MOTORB-2
  N2: M1.pin_2, MOTOR_SHIELD1.MOTORB-1
  N3: M2.pin_1, MOTOR_SHIELD1.MOTORA-2
  N4: M2.pin_2, MOTOR_SHIELD1.MOTORA-1

custom parts:
  Battery: Your standard 2x 18650 battery pack (7.4 Volts)
  FunduMoto Keyes L298P Motor Shield: FunduMoto / Keyes L298P Arduino motor driver shield - dual H-bridge, motor screw terminals, servo / ultrasonic / bluetooth / analog sensor headers.
