# Fritzing sketch ch16_enoder_2wheel_robot (saved by Fritzing 1.0.8)
breadboards: 1

parts:
  VCC1 = Battery
  Part1 = Arduino Uno (Rev3) - ICSP
  PWMA = Motor Driver 1A Dual TB6612FNG
  M1 = gear-motor
  M2 = gear-motor
  Enc1 = shaft encoder
  Enc2 = shaft encoder

nets:
  GND: VCC1.-, Part1.GND, PWMA.GND, Enc1.GND, Enc2.GND
  N1: Part1.D8, PWMA.BIN2
  N2: Part1.D9_PWM, PWMA.PWMB
  N3: Part1.D11_PWM/MOSI, PWMA.PWMA
  N4: Part1.D2, Enc2.OUT
  N5: Part1.D3_PWM, Enc1.OUT
  N6: Part1.D4, PWMA.AIN2
  N7: Part1.D5_PWM, PWMA.AIN1
  N8: Part1.D6_PWM, PWMA.STBY
  N9: Part1.D7, PWMA.BIN1
  N10: Part1.VIN, PWMA.VM
  N11: PWMA.B02, M1.pin_2
  N12: PWMA.A02, M2.pin_1
  N13: PWMA.A01, M2.pin_2
  VCC: Enc1.VCC, Enc2.VCC

custom parts:
  Battery: Your standard 2x 18650 battery pack (7.4 Volts)
