# Fritzing sketch ch18_4axis_robot_arm (saved by Fritzing 1.0.8)
breadboards: 1

parts:
  VCC1 = 4 x AAA Battery Mount [internal_resistance=0.1Ω]
  Part1 = Arduino Uno (Rev3) - ICSP
  J5 = Basic Servo
  SERVO1 = Tower Pro SG90 servo [part_number=101246]
  SERVO2 = Tower Pro SG90 servo [part_number=101246]
  SERVO3 = Tower Pro SG90 servo [part_number=101246]

nets:
  GND: VCC1.-, J5.gnd, SERVO1.GND, SERVO2.GND, SERVO3.GND
  +5V: VCC1.+, J5.vcc, SERVO1.+5V, SERVO2.+5V, SERVO3.+5V
  N1: Part1.D9_PWM, SERVO2.Signal
  N2: Part1.D3_PWM, J5.pulse
  N3: Part1.D5_PWM, SERVO1.Signal
  N4: Part1.D6_PWM, SERVO3.Signal

custom parts:
  Tower Pro SG90 servo: Original file by John De Cristofaro http://www.adafruit.com/products/1449 Adafruit Feedback Servo (Small) Edited by: e-radionica.com 28/9/2015
